// Logisim project BFS.circ as structural Verilog: 6 circuits, main circuit main
module main (
  input  CLEAR,
  input  [3:0] wrt_adr,
  input  [3:0] wrt_value,
  input  [3:0] in_4,
  input  in_5,
  input  in_6,
  output [3:0] out_7,
  output BFS_COMPLETE,
  output [3:0] out_9,
  output [3:0] out_10
);

  wire adder_1_cout, and_1_out, and_2_out, and_3_out, and_4_out, and_5_out, clock_1_out, comparator_1_lt,
       graph_1_list_end, not_1_out, not_2_out, not_3_out, not_4_out, not_5_out, not_6_out, or_1_out,
       or_2_out, or_3_out, register_file_1_value_1;
  wire [3:0] adder_1_out, distances_1_value2, distances_1_value_1, multiplexer_1_out, multiplexer_2_out,
       multiplexer_3_out, multiplexer_4_out;

  Clock clock_1 (.out(clock_1_out));
  and and_1 (and_1_out, not_5_out, not_1_out);
  not not_1 (not_1_out, register_file_1_value_1);
  not not_2 (not_2_out, in_5);
  not not_3 (not_3_out, graph_1_list_end);
  or or_1 (or_1_out, and_1_out, in_5);
  and and_2 (and_2_out, graph_1_list_end, and_4_out);
  and and_3 (and_3_out, not_3_out, or_1_out);
  Multiplexer #(.width(4)) multiplexer_1 (.in0(out_7), .in1(in_4), .out(multiplexer_1_out), .sel(in_5));  // open: en
  queue queue_1 (
    .reg_write(and_3_out), .shift(and_2_out), .\input (multiplexer_1_out), .queue_top(out_9),
    .queue_end(BFS_COMPLETE), .CLK(clock_1_out), .clear(CLEAR), .queue_read(not_2_out));
  not not_4 (not_4_out, in_5);
  not not_5 (not_5_out, in_6);
  and and_4 (and_4_out, not_5_out, not_4_out);
  not not_6 (not_6_out, graph_1_list_end);
  graph graph_1 (
    .read_adr(out_9), .wrt_adr(wrt_adr), .CLK(clock_1_out), .Input(wrt_value), .value(out_7),
    .list_end(graph_1_list_end), .clear(CLEAR), .graph_read(and_4_out), .graph_write(in_6));
  and and_5 (and_5_out, not_6_out, and_4_out);
  or or_2 (or_2_out, and_5_out, in_5);
  distances distances_1 (
    .Read_adr1(multiplexer_4_out), .RegRead(or_2_out), .regWrite(or_2_out), .write_addr(multiplexer_4_out),
    .read_adr2(out_9), .\input (multiplexer_2_out), .CLK(clock_1_out), .RegClear(CLEAR),
    .Value_1(distances_1_value_1), .value2(distances_1_value2));
  register_file register_file_1 (
    .Read_adr(multiplexer_4_out), .RegRead(or_2_out), .regWrite(or_2_out), .write_addr(multiplexer_4_out),
    .\input (or_2_out), .CLK(clock_1_out), .RegClear(CLEAR), .Value_1(register_file_1_value_1));
  Adder #(.width(4)) adder_1 (
    .a(distances_1_value2), .b(4'b0001), .out(adder_1_out), .cout(adder_1_cout));  // open: cin
  Multiplexer #(.width(4)) multiplexer_2 (
    .in0(multiplexer_3_out), .in1(4'b0000), .out(multiplexer_2_out), .sel(in_5));  // open: en
  Multiplexer #(.width(4)) multiplexer_3 (
    .in0(adder_1_out), .in1(distances_1_value_1), .out(multiplexer_3_out), .sel(or_3_out));  // open: en
  Multiplexer #(.width(4)) multiplexer_4 (.in0(out_7), .in1(in_4), .out(multiplexer_4_out), .sel(in_5));  // open: en
  Comparator #(.width(4), .mode("unsigned")) comparator_1 (
    .a(distances_1_value_1), .b(adder_1_out), .lt(comparator_1_lt));  // open: gt, eq
  or or_3 (or_3_out, comparator_1_lt, adder_1_cout);

  assign out_10 = out_9;
endmodule

module register_file (
  input  [3:0] Read_adr,
  input  RegRead,
  input  regWrite,
  input  [3:0] write_addr,
  input  \input ,
  input  CLK,
  input  RegClear,
  output Value_1
);

  wire decoder_1_out0, decoder_1_out1, decoder_1_out2, decoder_1_out3, decoder_1_out4, decoder_1_out5,
       decoder_1_out6, decoder_1_out7, decoder_1_out8, decoder_1_out9, decoder_1_out10, decoder_1_out11,
       decoder_1_out12, decoder_1_out13, decoder_1_out14, decoder_1_out15, s0_q, s1_q, s2_q, s3_q, s4_q,
       s5_q, s6_q, s7_q, t0_q, t1_q, t2_q, t3_q, t4_q, t5_q, t6_q, t7_q;

  Decoder #(.select(4), .disabled(0)) decoder_1 (
    .out0(decoder_1_out0), .out1(decoder_1_out1), .out2(decoder_1_out2), .out3(decoder_1_out3),
    .out4(decoder_1_out4), .out5(decoder_1_out5), .out6(decoder_1_out6), .out7(decoder_1_out7),
    .out8(decoder_1_out8), .out9(decoder_1_out9), .out10(decoder_1_out10), .out11(decoder_1_out11),
    .out12(decoder_1_out12), .out13(decoder_1_out13), .out14(decoder_1_out14), .out15(decoder_1_out15),
    .sel(write_addr), .en(regWrite));
  Register #(.width(1)) t0 (.D(\input ), .en(decoder_1_out0), .Q(t0_q), .clk(CLK), .clr(RegClear));
  Register #(.width(1)) t1 (.D(\input ), .en(decoder_1_out1), .Q(t1_q), .clk(CLK), .clr(RegClear));
  Register #(.width(1)) t2 (.D(\input ), .en(decoder_1_out2), .Q(t2_q), .clk(CLK), .clr(RegClear));
  Register #(.width(1)) t3 (.D(\input ), .en(decoder_1_out3), .Q(t3_q), .clk(CLK), .clr(RegClear));
  Register #(.width(1)) t4 (.D(\input ), .en(decoder_1_out4), .Q(t4_q), .clk(CLK), .clr(RegClear));
  Register #(.width(1)) t5 (.D(\input ), .en(decoder_1_out5), .Q(t5_q), .clk(CLK), .clr(RegClear));
  Register #(.width(1)) t6 (.D(\input ), .en(decoder_1_out6), .Q(t6_q), .clk(CLK), .clr(RegClear));
  Register #(.width(1)) t7 (.D(\input ), .en(decoder_1_out7), .Q(t7_q), .clk(CLK), .clr(RegClear));
  Register #(.width(1)) s0 (.D(\input ), .en(decoder_1_out8), .Q(s0_q), .clk(CLK), .clr(RegClear));
  Register #(.width(1)) s1 (.D(\input ), .en(decoder_1_out9), .Q(s1_q), .clk(CLK), .clr(RegClear));
  Register #(.width(1)) s2 (.D(\input ), .en(decoder_1_out10), .Q(s2_q), .clk(CLK), .clr(RegClear));
  Register #(.width(1)) s3 (.D(\input ), .en(decoder_1_out11), .Q(s3_q), .clk(CLK), .clr(RegClear));
  Register #(.width(1)) s4 (.D(\input ), .en(decoder_1_out12), .Q(s4_q), .clk(CLK), .clr(RegClear));
  Register #(.width(1)) s5 (.D(\input ), .en(decoder_1_out13), .Q(s5_q), .clk(CLK), .clr(RegClear));
  Register #(.width(1)) s6 (.D(\input ), .en(decoder_1_out14), .Q(s6_q), .clk(CLK), .clr(RegClear));
  Register #(.width(1)) s7 (.D(\input ), .en(decoder_1_out15), .Q(s7_q), .clk(CLK), .clr(RegClear));
  Multiplexer #(.select(4), .disabled(0)) multiplexer_1 (
    .in0(t0_q), .in1(t1_q), .in2(t2_q), .in3(t3_q), .in4(t4_q), .in5(t5_q), .in6(t6_q), .in7(t7_q),
    .in8(s0_q), .in9(s1_q), .in10(s2_q), .in11(s3_q), .in12(s4_q), .in13(s5_q), .in14(s6_q), .in15(s7_q),
    .out(Value_1), .sel(Read_adr), .en(RegRead));
endmodule

module adj_lst (
  input  RegRead,
  input  regWrite,
  input  [3:0] \input ,
  input  CLK,
  input  RegClear,
  output [3:0] Value_1,
  output list_end
);

  wire decoder_1_out0, decoder_1_out1, decoder_1_out2, decoder_1_out3, decoder_1_out4, decoder_1_out5,
       decoder_1_out6, decoder_1_out7, decoder_1_out8, decoder_1_out9, decoder_1_out10, decoder_1_out11,
       decoder_1_out12, decoder_1_out13, decoder_1_out14, decoder_1_out15;
  wire [3:0] adder_1_out, adder_2_out, cnt_q, s0_q, s1_q, s2_q, s3_q, s4_q, s5_q, s6_q, s7_q, t0_q, t1_q,
       t2_q, t3_q, t4_q, t5_q, t6_q, t7_q, write_adr_q;

  Register #(.width(4)) write_adr (.D(adder_1_out), .en(regWrite), .Q(write_adr_q), .clk(CLK), .clr(RegClear));
  Decoder #(.select(4), .disabled(0)) decoder_1 (
    .out0(decoder_1_out0), .out1(decoder_1_out1), .out2(decoder_1_out2), .out3(decoder_1_out3),
    .out4(decoder_1_out4), .out5(decoder_1_out5), .out6(decoder_1_out6), .out7(decoder_1_out7),
    .out8(decoder_1_out8), .out9(decoder_1_out9), .out10(decoder_1_out10), .out11(decoder_1_out11),
    .out12(decoder_1_out12), .out13(decoder_1_out13), .out14(decoder_1_out14), .out15(decoder_1_out15),
    .sel(write_adr_q), .en(regWrite));
  Adder #(.width(4)) adder_1 (.a(write_adr_q), .b(4'b0001), .out(adder_1_out));  // open: cin, cout
  Register #(.width(4)) t0 (.D(\input ), .en(decoder_1_out0), .Q(t0_q), .clk(CLK), .clr(RegClear));
  Register #(.width(4)) t1 (.D(\input ), .en(decoder_1_out1), .Q(t1_q), .clk(CLK), .clr(RegClear));
  Register #(.width(4)) t2 (.D(\input ), .en(decoder_1_out2), .Q(t2_q), .clk(CLK), .clr(RegClear));
  Register #(.width(4)) t3 (.D(\input ), .en(decoder_1_out3), .Q(t3_q), .clk(CLK), .clr(RegClear));
  Register #(.width(4)) t4 (.D(\input ), .en(decoder_1_out4), .Q(t4_q), .clk(CLK), .clr(RegClear));
  Register #(.width(4)) t5 (.D(\input ), .en(decoder_1_out5), .Q(t5_q), .clk(CLK), .clr(RegClear));
  Register #(.width(4)) t6 (.D(\input ), .en(decoder_1_out6), .Q(t6_q), .clk(CLK), .clr(RegClear));
  Register #(.width(4)) t7 (.D(\input ), .en(decoder_1_out7), .Q(t7_q), .clk(CLK), .clr(RegClear));
  Register #(.width(4)) s0 (.D(\input ), .en(decoder_1_out8), .Q(s0_q), .clk(CLK), .clr(RegClear));
  Register #(.width(4)) s1 (.D(\input ), .en(decoder_1_out9), .Q(s1_q), .clk(CLK), .clr(RegClear));
  Register #(.width(4)) s2 (.D(\input ), .en(decoder_1_out10), .Q(s2_q), .clk(CLK), .clr(RegClear));
  Register #(.width(4)) s3 (.D(\input ), .en(decoder_1_out11), .Q(s3_q), .clk(CLK), .clr(RegClear));
  Register #(.width(4)) s4 (.D(\input ), .en(decoder_1_out12), .Q(s4_q), .clk(CLK), .clr(RegClear));
  Register #(.width(4)) s5 (.D(\input ), .en(decoder_1_out13), .Q(s5_q), .clk(CLK), .clr(RegClear));
  Register #(.width(4)) s6 (.D(\input ), .en(decoder_1_out14), .Q(s6_q), .clk(CLK), .clr(RegClear));
  Register #(.width(4)) s7 (.D(\input ), .en(decoder_1_out15), .Q(s7_q), .clk(CLK), .clr(RegClear));
  Multiplexer #(.select(4), .width(4), .disabled(0)) multiplexer_1 (
    .in0(t0_q), .in1(t1_q), .in2(t2_q), .in3(t3_q), .in4(t4_q), .in5(t5_q), .in6(t6_q), .in7(t7_q),
    .in8(s0_q), .in9(s1_q), .in10(s2_q), .in11(s3_q), .in12(s4_q), .in13(s5_q), .in14(s6_q), .in15(s7_q),
    .out(Value_1), .sel(cnt_q), .en(RegRead));
  Register #(.width(4)) cnt (.D(adder_2_out), .en(RegRead), .Q(cnt_q), .clk(CLK), .clr(RegClear));
  Adder #(.width(4)) adder_2 (.a(cnt_q), .b(4'b0001), .out(adder_2_out));  // open: cin, cout
  Comparator #(.width(4)) comparator_1 (.a(cnt_q), .b(write_adr_q), .eq(list_end));  // open: gt, lt
  Adder #(.width(4)) adder_3 ();  // open: a, b, out, cin, cout
endmodule

module queue (
  input  queue_read,
  input  reg_write,
  input  CLK,
  input  shift,
  input  clear,
  input  [3:0] \input ,
  output [3:0] queue_top,
  output queue_end
);

  wire decoder_1_out0, decoder_1_out1, decoder_1_out2, decoder_1_out3, decoder_1_out4, decoder_1_out5,
       decoder_1_out6, decoder_1_out7, decoder_1_out8, decoder_1_out9, decoder_1_out10, decoder_1_out11,
       decoder_1_out12, decoder_1_out13, decoder_1_out14, decoder_1_out15, or_1_out, or_2_out, or_3_out,
       or_4_out, or_5_out, or_6_out, or_7_out, or_8_out, or_9_out, or_10_out, or_11_out, or_12_out,
       or_13_out, or_14_out, or_15_out, or_16_out, or_17_out;
  wire [3:0] adder_1_out, multiplexer_1_out, multiplexer_2_out, multiplexer_3_out, multiplexer_4_out,
       multiplexer_5_out, multiplexer_6_out, multiplexer_7_out, multiplexer_8_out, multiplexer_9_out,
       multiplexer_10_out, multiplexer_11_out, multiplexer_12_out, multiplexer_13_out, multiplexer_14_out,
       multiplexer_15_out, multiplexer_16_out, multiplexer_17_out, register_1_q, register_2_q, register_3_q,
       register_4_q, register_5_q, register_6_q, register_7_q, register_8_q, register_9_q, register_10_q,
       register_11_q, register_12_q, register_13_q, register_14_q, register_15_q, register_16_q,
       subtractor_1_out, write_adr_q;

  Register #(.width(4)) write_adr (.D(multiplexer_1_out), .en(or_1_out), .Q(write_adr_q), .clk(CLK), .clr(clear));
  or or_1 (or_1_out, reg_write, shift);
  Decoder #(.select(4), .disabled(0)) decoder_1 (
    .out0(decoder_1_out0), .out1(decoder_1_out1), .out2(decoder_1_out2), .out3(decoder_1_out3),
    .out4(decoder_1_out4), .out5(decoder_1_out5), .out6(decoder_1_out6), .out7(decoder_1_out7),
    .out8(decoder_1_out8), .out9(decoder_1_out9), .out10(decoder_1_out10), .out11(decoder_1_out11),
    .out12(decoder_1_out12), .out13(decoder_1_out13), .out14(decoder_1_out14), .out15(decoder_1_out15),
    .sel(write_adr_q), .en(reg_write));
  Multiplexer #(.width(4), .enable("false")) multiplexer_1 (
    .in0(adder_1_out), .in1(subtractor_1_out), .out(multiplexer_1_out), .sel(shift));
  Adder #(.width(4)) adder_1 (.a(write_adr_q), .b(4'b0001), .out(adder_1_out));  // open: cin, cout
  Subtractor #(.width(4)) subtractor_1 (.a(write_adr_q), .b(4'b0001), .out(subtractor_1_out));  // open: bin, bout
  or or_2 (or_2_out, decoder_1_out0, shift);
  or or_3 (or_3_out, decoder_1_out1, shift);
  or or_4 (or_4_out, decoder_1_out2, shift);
  or or_5 (or_5_out, decoder_1_out3, shift);
  or or_6 (or_6_out, decoder_1_out4, shift);
  or or_7 (or_7_out, decoder_1_out5, shift);
  or or_8 (or_8_out, shift, decoder_1_out6);
  or or_9 (or_9_out, shift, decoder_1_out7);
  or or_10 (or_10_out, shift, decoder_1_out8);
  or or_11 (or_11_out, decoder_1_out9, shift);
  or or_12 (or_12_out, shift, decoder_1_out10);
  or or_13 (or_13_out, shift, decoder_1_out11);
  or or_14 (or_14_out, shift, decoder_1_out12);
  or or_15 (or_15_out, shift, decoder_1_out13);
  or or_16 (or_16_out, shift, decoder_1_out14);
  or or_17 (or_17_out, shift, decoder_1_out15);
  Multiplexer #(.width(4)) multiplexer_2 (
    .in0(\input ), .in1(register_2_q), .out(multiplexer_2_out), .sel(shift));  // open: en
  Multiplexer #(.width(4)) multiplexer_3 (
    .in0(\input ), .in1(register_3_q), .out(multiplexer_3_out), .sel(shift));  // open: en
  Multiplexer #(.width(4)) multiplexer_4 (
    .in0(\input ), .in1(register_4_q), .out(multiplexer_4_out), .sel(shift));  // open: en
  Multiplexer #(.width(4)) multiplexer_5 (
    .in0(\input ), .in1(register_5_q), .out(multiplexer_5_out), .sel(shift));  // open: en
  Multiplexer #(.width(4)) multiplexer_6 (
    .in0(\input ), .in1(register_6_q), .out(multiplexer_6_out), .sel(shift));  // open: en
  Multiplexer #(.width(4)) multiplexer_7 (
    .in0(\input ), .in1(register_7_q), .out(multiplexer_7_out), .sel(shift));  // open: en
  Multiplexer #(.width(4)) multiplexer_8 (
    .in0(\input ), .in1(register_8_q), .out(multiplexer_8_out), .sel(shift));  // open: en
  Multiplexer #(.width(4)) multiplexer_9 (
    .in0(\input ), .in1(register_9_q), .out(multiplexer_9_out), .sel(shift));  // open: en
  Multiplexer #(.width(4)) multiplexer_10 (
    .in0(\input ), .in1(register_10_q), .out(multiplexer_10_out), .sel(shift));  // open: en
  Multiplexer #(.width(4)) multiplexer_11 (
    .in0(\input ), .in1(register_11_q), .out(multiplexer_11_out), .sel(shift));  // open: en
  Multiplexer #(.width(4)) multiplexer_12 (
    .in0(\input ), .in1(register_12_q), .out(multiplexer_12_out), .sel(shift));  // open: en
  Multiplexer #(.width(4)) multiplexer_13 (
    .in0(\input ), .in1(register_13_q), .out(multiplexer_13_out), .sel(shift));  // open: en
  Multiplexer #(.width(4)) multiplexer_14 (
    .in0(\input ), .in1(register_14_q), .out(multiplexer_14_out), .sel(shift));  // open: en
  Multiplexer #(.width(4)) multiplexer_15 (
    .in0(\input ), .in1(register_15_q), .out(multiplexer_15_out), .sel(shift));  // open: en
  Multiplexer #(.width(4)) multiplexer_16 (
    .in0(\input ), .in1(register_16_q), .out(multiplexer_16_out), .sel(shift));  // open: en
  Multiplexer #(.width(4), .enable("false")) multiplexer_17 (
    .in0(\input ), .in1(4'b0000), .out(multiplexer_17_out), .sel(shift));
  Register #(.width(4)) register_1 (.D(multiplexer_2_out), .en(or_2_out), .Q(register_1_q), .clk(CLK), .clr(clear));
  Register #(.width(4)) register_2 (.D(multiplexer_3_out), .en(or_3_out), .Q(register_2_q), .clk(CLK), .clr(clear));
  Register #(.width(4)) register_3 (.D(multiplexer_4_out), .en(or_4_out), .Q(register_3_q), .clk(CLK), .clr(clear));
  Register #(.width(4)) register_4 (.D(multiplexer_5_out), .en(or_5_out), .Q(register_4_q), .clk(CLK), .clr(clear));
  Register #(.width(4)) register_5 (.D(multiplexer_6_out), .en(or_6_out), .Q(register_5_q), .clk(CLK), .clr(clear));
  Register #(.width(4)) register_6 (.D(multiplexer_7_out), .en(or_7_out), .Q(register_6_q), .clk(CLK), .clr(clear));
  Register #(.width(4)) register_7 (.D(multiplexer_8_out), .en(or_8_out), .Q(register_7_q), .clk(CLK), .clr(clear));
  Register #(.width(4)) register_8 (.D(multiplexer_9_out), .en(or_9_out), .Q(register_8_q), .clk(CLK), .clr(clear));
  Register #(.width(4)) register_9 (.D(multiplexer_10_out), .en(or_10_out), .Q(register_9_q), .clk(CLK), .clr(clear));
  Register #(.width(4)) register_10 (.D(multiplexer_11_out), .en(or_11_out), .Q(register_10_q), .clk(CLK), .clr(clear));
  Register #(.width(4)) register_11 (.D(multiplexer_12_out), .en(or_12_out), .Q(register_11_q), .clk(CLK), .clr(clear));
  Register #(.width(4)) register_12 (.D(multiplexer_13_out), .en(or_13_out), .Q(register_12_q), .clk(CLK), .clr(clear));
  Register #(.width(4)) register_13 (.D(multiplexer_14_out), .en(or_14_out), .Q(register_13_q), .clk(CLK), .clr(clear));
  Register #(.width(4)) register_14 (.D(multiplexer_15_out), .en(or_15_out), .Q(register_14_q), .clk(CLK), .clr(clear));
  Register #(.width(4)) register_15 (.D(multiplexer_16_out), .en(or_16_out), .Q(register_15_q), .clk(CLK), .clr(clear));
  Register #(.width(4)) register_16 (.D(multiplexer_17_out), .en(or_17_out), .Q(register_16_q), .clk(CLK), .clr(clear));
  Multiplexer #(.width(4)) multiplexer_18 (
    .in0(4'b0000), .in1(register_1_q), .out(queue_top), .sel(queue_read));  // open: en
  Comparator #(.width(4)) comparator_1 (.a(4'b0000), .b(write_adr_q), .eq(queue_end));  // open: gt, lt
endmodule

module graph (
  input  graph_read,
  input  graph_write,
  input  [3:0] read_adr,
  input  [3:0] wrt_adr,
  input  CLK,
  input  [3:0] Input,
  input  clear,
  output [3:0] value,
  output list_end
);

  wire adj_lst_1_list_end, adj_lst_2_list_end, adj_lst_3_list_end, adj_lst_4_list_end, adj_lst_5_list_end,
       adj_lst_6_list_end, adj_lst_7_list_end, adj_lst_8_list_end, adj_lst_9_list_end, adj_lst_10_list_end,
       adj_lst_11_list_end, adj_lst_12_list_end, adj_lst_13_list_end, adj_lst_14_list_end,
       adj_lst_15_list_end, adj_lst_16_list_end, decoder_1_out0, decoder_1_out1, decoder_1_out2,
       decoder_1_out3, decoder_1_out4, decoder_1_out5, decoder_1_out6, decoder_1_out7, decoder_1_out8,
       decoder_1_out9, decoder_1_out10, decoder_1_out11, decoder_1_out12, decoder_1_out13, decoder_1_out14,
       decoder_1_out15, decoder_2_out0, decoder_2_out1, decoder_2_out2, decoder_2_out3, decoder_2_out4,
       decoder_2_out5, decoder_2_out6, decoder_2_out7, decoder_2_out8, decoder_2_out9, decoder_2_out10,
       decoder_2_out11, decoder_2_out12, decoder_2_out13, decoder_2_out14, decoder_2_out15;
  wire [3:0] adj_lst_1_value_1, adj_lst_2_value_1, adj_lst_3_value_1, adj_lst_4_value_1, adj_lst_5_value_1,
       adj_lst_6_value_1, adj_lst_7_value_1, adj_lst_8_value_1, adj_lst_9_value_1, adj_lst_10_value_1,
       adj_lst_11_value_1, adj_lst_12_value_1, adj_lst_13_value_1, adj_lst_14_value_1, adj_lst_15_value_1,
       adj_lst_16_value_1;

  Decoder #(.select(4), .disabled(0)) decoder_1 (
    .out0(decoder_1_out0), .out1(decoder_1_out1), .out2(decoder_1_out2), .out3(decoder_1_out3),
    .out4(decoder_1_out4), .out5(decoder_1_out5), .out6(decoder_1_out6), .out7(decoder_1_out7),
    .out8(decoder_1_out8), .out9(decoder_1_out9), .out10(decoder_1_out10), .out11(decoder_1_out11),
    .out12(decoder_1_out12), .out13(decoder_1_out13), .out14(decoder_1_out14), .out15(decoder_1_out15),
    .sel(read_adr), .en(graph_read));
  Decoder #(.select(4), .disabled(0)) decoder_2 (
    .out0(decoder_2_out0), .out1(decoder_2_out1), .out2(decoder_2_out2), .out3(decoder_2_out3),
    .out4(decoder_2_out4), .out5(decoder_2_out5), .out6(decoder_2_out6), .out7(decoder_2_out7),
    .out8(decoder_2_out8), .out9(decoder_2_out9), .out10(decoder_2_out10), .out11(decoder_2_out11),
    .out12(decoder_2_out12), .out13(decoder_2_out13), .out14(decoder_2_out14), .out15(decoder_2_out15),
    .sel(wrt_adr), .en(graph_write));
  adj_lst adj_lst_1 (
    .RegRead(decoder_1_out0), .regWrite(decoder_2_out0), .\input (Input), .CLK(CLK), .RegClear(clear),
    .Value_1(adj_lst_1_value_1), .list_end(adj_lst_1_list_end));
  adj_lst adj_lst_2 (
    .RegRead(decoder_1_out1), .regWrite(decoder_2_out1), .\input (Input), .CLK(CLK), .RegClear(clear),
    .Value_1(adj_lst_2_value_1), .list_end(adj_lst_2_list_end));
  adj_lst adj_lst_3 (
    .RegRead(decoder_1_out2), .regWrite(decoder_2_out2), .\input (Input), .CLK(CLK), .RegClear(clear),
    .Value_1(adj_lst_3_value_1), .list_end(adj_lst_3_list_end));
  adj_lst adj_lst_4 (
    .RegRead(decoder_1_out3), .regWrite(decoder_2_out3), .\input (Input), .CLK(CLK), .RegClear(clear),
    .Value_1(adj_lst_4_value_1), .list_end(adj_lst_4_list_end));
  adj_lst adj_lst_5 (
    .RegRead(decoder_1_out4), .regWrite(decoder_2_out4), .\input (Input), .CLK(CLK), .RegClear(clear),
    .Value_1(adj_lst_5_value_1), .list_end(adj_lst_5_list_end));
  adj_lst adj_lst_6 (
    .RegRead(decoder_1_out5), .regWrite(decoder_2_out5), .\input (Input), .CLK(CLK), .RegClear(clear),
    .Value_1(adj_lst_6_value_1), .list_end(adj_lst_6_list_end));
  adj_lst adj_lst_7 (
    .RegRead(decoder_1_out6), .regWrite(decoder_2_out6), .\input (Input), .CLK(CLK), .RegClear(clear),
    .Value_1(adj_lst_7_value_1), .list_end(adj_lst_7_list_end));
  adj_lst adj_lst_8 (
    .RegRead(decoder_1_out7), .regWrite(decoder_2_out7), .\input (Input), .CLK(CLK), .RegClear(clear),
    .Value_1(adj_lst_8_value_1), .list_end(adj_lst_8_list_end));
  adj_lst adj_lst_9 (
    .RegRead(decoder_1_out8), .regWrite(decoder_2_out8), .\input (Input), .CLK(CLK), .RegClear(clear),
    .Value_1(adj_lst_9_value_1), .list_end(adj_lst_9_list_end));
  adj_lst adj_lst_10 (
    .RegRead(decoder_1_out9), .regWrite(decoder_2_out9), .\input (Input), .CLK(CLK), .RegClear(clear),
    .Value_1(adj_lst_10_value_1), .list_end(adj_lst_10_list_end));
  adj_lst adj_lst_11 (
    .RegRead(decoder_1_out10), .regWrite(decoder_2_out10), .\input (Input), .CLK(CLK), .RegClear(clear),
    .Value_1(adj_lst_11_value_1), .list_end(adj_lst_11_list_end));
  adj_lst adj_lst_12 (
    .RegRead(decoder_1_out11), .regWrite(decoder_2_out11), .\input (Input), .CLK(CLK), .RegClear(clear),
    .Value_1(adj_lst_12_value_1), .list_end(adj_lst_12_list_end));
  adj_lst adj_lst_13 (
    .RegRead(decoder_1_out12), .regWrite(decoder_2_out12), .\input (Input), .CLK(CLK), .RegClear(clear),
    .Value_1(adj_lst_13_value_1), .list_end(adj_lst_13_list_end));
  adj_lst adj_lst_14 (
    .RegRead(decoder_1_out13), .regWrite(decoder_2_out13), .\input (Input), .CLK(CLK), .RegClear(clear),
    .Value_1(adj_lst_14_value_1), .list_end(adj_lst_14_list_end));
  adj_lst adj_lst_15 (
    .RegRead(decoder_1_out14), .regWrite(decoder_2_out14), .\input (Input), .CLK(CLK), .RegClear(clear),
    .Value_1(adj_lst_15_value_1), .list_end(adj_lst_15_list_end));
  adj_lst adj_lst_16 (
    .RegRead(decoder_1_out15), .regWrite(decoder_2_out15), .\input (Input), .CLK(CLK), .RegClear(clear),
    .Value_1(adj_lst_16_value_1), .list_end(adj_lst_16_list_end));
  Multiplexer #(.select(4), .width(4), .disabled(0)) multiplexer_1 (
    .in0(adj_lst_1_value_1), .in1(adj_lst_2_value_1), .in2(adj_lst_3_value_1), .in3(adj_lst_4_value_1),
    .in4(adj_lst_5_value_1), .in5(adj_lst_6_value_1), .in6(adj_lst_7_value_1), .in7(adj_lst_8_value_1),
    .in8(adj_lst_9_value_1), .in9(adj_lst_10_value_1), .in10(adj_lst_11_value_1), .in11(adj_lst_12_value_1),
    .in12(adj_lst_13_value_1), .in13(adj_lst_14_value_1), .in14(adj_lst_15_value_1),
    .in15(adj_lst_16_value_1), .out(value), .sel(read_adr), .en(graph_read));
  Multiplexer #(.select(4), .disabled(0)) multiplexer_2 (
    .in0(adj_lst_1_list_end), .in1(adj_lst_2_list_end), .in2(adj_lst_3_list_end), .in3(adj_lst_4_list_end),
    .in4(adj_lst_5_list_end), .in5(adj_lst_6_list_end), .in6(adj_lst_7_list_end), .in7(adj_lst_8_list_end),
    .in8(adj_lst_9_list_end), .in9(adj_lst_10_list_end), .in10(adj_lst_11_list_end),
    .in11(adj_lst_12_list_end), .in12(adj_lst_13_list_end), .in13(adj_lst_14_list_end),
    .in14(adj_lst_15_list_end), .in15(adj_lst_16_list_end), .out(list_end), .sel(read_adr), .en(graph_read));
endmodule

module distances (
  input  [3:0] Read_adr1,
  input  RegRead,
  input  regWrite,
  input  [3:0] write_addr,
  input  [3:0] read_adr2,
  input  [3:0] \input ,
  input  CLK,
  input  RegClear,
  output [3:0] Value_1,
  output [3:0] value2
);

  wire decoder_1_out0, decoder_1_out1, decoder_1_out2, decoder_1_out3, decoder_1_out4, decoder_1_out5,
       decoder_1_out6, decoder_1_out7, decoder_1_out8, decoder_1_out9, decoder_1_out10, decoder_1_out11,
       decoder_1_out12, decoder_1_out13, decoder_1_out14, decoder_1_out15, or_1_out, or_2_out, or_3_out,
       or_4_out, or_5_out, or_6_out, or_7_out, or_8_out, or_9_out, or_10_out, or_11_out, or_12_out,
       or_13_out, or_14_out, or_15_out, or_16_out;
  wire [3:0] multiplexer_1_out, s0_q, s1_q, s2_q, s3_q, s4_q, s5_q, s6_q, s7_q, t0_q, t1_q, t2_q, t3_q, t4_q,
       t5_q, t6_q, t7_q;

  Decoder #(.select(4), .disabled(0)) decoder_1 (
    .out0(decoder_1_out0), .out1(decoder_1_out1), .out2(decoder_1_out2), .out3(decoder_1_out3),
    .out4(decoder_1_out4), .out5(decoder_1_out5), .out6(decoder_1_out6), .out7(decoder_1_out7),
    .out8(decoder_1_out8), .out9(decoder_1_out9), .out10(decoder_1_out10), .out11(decoder_1_out11),
    .out12(decoder_1_out12), .out13(decoder_1_out13), .out14(decoder_1_out14), .out15(decoder_1_out15),
    .sel(write_addr), .en(regWrite));
  or or_1 (or_1_out, decoder_1_out0, RegClear);
  or or_2 (or_2_out, decoder_1_out1, RegClear);
  or or_3 (or_3_out, decoder_1_out2, RegClear);
  or or_4 (or_4_out, decoder_1_out3, RegClear);
  or or_5 (or_5_out, decoder_1_out4, RegClear);
  or or_6 (or_6_out, decoder_1_out5, RegClear);
  or or_7 (or_7_out, decoder_1_out6, RegClear);
  or or_8 (or_8_out, decoder_1_out7, RegClear);
  or or_9 (or_9_out, decoder_1_out8, RegClear);
  or or_10 (or_10_out, RegClear, decoder_1_out9);
  or or_11 (or_11_out, RegClear, decoder_1_out10);
  or or_12 (or_12_out, RegClear, decoder_1_out11);
  or or_13 (or_13_out, RegClear, decoder_1_out12);
  or or_14 (or_14_out, RegClear, decoder_1_out13);
  or or_15 (or_15_out, RegClear, decoder_1_out14);
  or or_16 (or_16_out, RegClear, decoder_1_out15);
  Multiplexer #(.width(4)) multiplexer_1 (
    .in0(\input ), .in1(4'b1111), .out(multiplexer_1_out), .sel(RegClear));  // open: en
  Register #(.width(4)) t0 (.D(multiplexer_1_out), .en(or_1_out), .Q(t0_q), .clk(CLK), .clr(1'b0));
  Register #(.width(4)) t1 (.D(multiplexer_1_out), .en(or_2_out), .Q(t1_q), .clk(CLK), .clr(1'b0));
  Register #(.width(4)) t2 (.D(multiplexer_1_out), .en(or_3_out), .Q(t2_q), .clk(CLK), .clr(1'b0));
  Register #(.width(4)) t3 (.D(multiplexer_1_out), .en(or_4_out), .Q(t3_q), .clk(CLK), .clr(1'b0));
  Register #(.width(4)) t4 (.D(multiplexer_1_out), .en(or_5_out), .Q(t4_q), .clk(CLK), .clr(1'b0));
  Register #(.width(4)) t5 (.D(multiplexer_1_out), .en(or_6_out), .Q(t5_q), .clk(CLK), .clr(1'b0));
  Register #(.width(4)) t6 (.D(multiplexer_1_out), .en(or_7_out), .Q(t6_q), .clk(CLK), .clr(1'b0));
  Register #(.width(4)) t7 (.D(multiplexer_1_out), .en(or_8_out), .Q(t7_q), .clk(CLK), .clr(1'b0));
  Register #(.width(4)) s0 (.D(multiplexer_1_out), .en(or_9_out), .Q(s0_q), .clk(CLK), .clr(1'b0));
  Register #(.width(4)) s1 (.D(multiplexer_1_out), .en(or_10_out), .Q(s1_q), .clk(CLK), .clr(1'b0));
  Register #(.width(4)) s2 (.D(multiplexer_1_out), .en(or_11_out), .Q(s2_q), .clk(CLK), .clr(1'b0));
  Register #(.width(4)) s3 (.D(multiplexer_1_out), .en(or_12_out), .Q(s3_q), .clk(CLK), .clr(1'b0));
  Register #(.width(4)) s4 (.D(multiplexer_1_out), .en(or_13_out), .Q(s4_q), .clk(CLK), .clr(1'b0));
  Register #(.width(4)) s5 (.D(multiplexer_1_out), .en(or_14_out), .Q(s5_q), .clk(CLK), .clr(1'b0));
  Register #(.width(4)) s6 (.D(multiplexer_1_out), .en(or_15_out), .Q(s6_q), .clk(CLK), .clr(1'b0));
  Register #(.width(4)) s7 (.D(multiplexer_1_out), .en(or_16_out), .Q(s7_q), .clk(CLK), .clr(1'b0));
  Multiplexer #(.select(4), .width(4), .disabled(0)) multiplexer_2 (
    .in0(t0_q), .in1(t1_q), .in2(t2_q), .in3(t3_q), .in4(t4_q), .in5(t5_q), .in6(t6_q), .in7(t7_q),
    .in8(s0_q), .in9(s1_q), .in10(s2_q), .in11(s3_q), .in12(s4_q), .in13(s5_q), .in14(s6_q), .in15(s7_q),
    .out(Value_1), .sel(Read_adr1), .en(RegRead));
  Multiplexer #(.select(4), .width(4), .disabled(0)) multiplexer_3 (
    .in0(t0_q), .in1(t1_q), .in2(t2_q), .in3(t3_q), .in4(t4_q), .in5(t5_q), .in6(t6_q), .in7(t7_q),
    .in8(s0_q), .in9(s1_q), .in10(s2_q), .in11(s3_q), .in12(s4_q), .in13(s5_q), .in14(s6_q), .in15(s7_q),
    .out(value2), .sel(read_adr2), .en(RegRead));
endmodule
